// Logisim project FA.circ as structural Verilog: 2 circuits, main circuit FA
module FA (
  input  A,
  input  B,
  input  CIN,
  output S,
  output COUT
);

  wire and_1_out, and_2_out, xor_1_out;

  and and_1 (and_1_out, B, A);
  xor xor_1 (xor_1_out, B, A);
  xor xor_2 (S, xor_1_out, CIN);
  and and_2 (and_2_out, xor_1_out, CIN);
  or or_1 (COUT, and_1_out, and_2_out);
endmodule

module ADDSUB4 (
  input  [3:0] A,
  input  [3:0] B,
  output C1,
  output [3:0] S,
  output C2,
  output C3,
  output C
);

  wire fa_1_cout, fa_2_cout, fa_3_cout;

  FA fa_1 (.A(A[0]), .B(A[0]), .CIN(fa_1_cout), .S(S[0]), .COUT(fa_1_cout));
  FA fa_2 (.A(A[1]), .B(B[1]), .CIN(fa_2_cout), .S(C1), .COUT(fa_2_cout));
  FA fa_3 (.A(A[2]), .B(A[2]), .CIN(fa_3_cout), .S(C2), .COUT(fa_3_cout));
  FA fa_4 (.A(A[3]), .B(B[3]), .CIN(C), .S(S[3]), .COUT(C));

  assign {B[2], B[0]} = {A[2], A[0]};
  assign C3 = C;
  assign S[2:1] = {C2, C1};
  // also tied to GND on the sheet: fa_1_cout
endmodule
